# Fritzing sketch Circuito_ToogleButton (saved by Fritzing 0.9.6b)
breadboards: 1

parts:
  Mod1 = Heltec WiFi LoRa 32 V2 [part_number=HTIT-WB32LA]
  R1 = Resistor [tolerance=±5% power=0.25 resistance=330 package=THT]
  LED1 = smd LED [color="Red (633nm)" package="0805 [SMD]"]
  R2 = Resistor [tolerance=±5% power=0.25 resistance=330 package=THT]
  S1 = Momentary Switch [package=ksa_sealed_tac_switch]

nets:
  N1: Mod1.pin_2, R1.Pin_0
  N2: Mod1.pin_16, Mod1.pin_17, R2.Pin_1
  N3: Mod1.GND, LED1.cathode, S1.2
  N4: Mod1.pin_21, Mod1.pin_22
  N5: Mod1.pin_34, R2.Pin_0, S1.4
  N6: R1.Pin_1, LED1.anode
